// Logisim project bfcpu.circ as structural Verilog: 5 circuits, main circuit main
module main (
);

  wire alu_1_nz, and_1_out, button_1_out, controllersim_1_art_par, controllersim_1_halted,
       controllersim_1_rclk, controllersim_1_wclk, demultiplexer_1_out1, demultiplexer_1_out2,
       demultiplexer_1_out3, demultiplexer_1_out4, demultiplexer_1_out5, demultiplexer_1_out6,
       demultiplexer_1_out7, not_1_out, or_1_out;
  wire [1:0] controllersim_1_opr;
  wire [2:0] controllersim_1_opnd;
  wire [6:0] keyboard_1_data;
  wire [7:0] alu_1_res, alu_1_res_2, controlled_buffer_1_out, controlled_buffer_2_out, controllersim_1_cycle,
       rom_1_data;
  wire [15:0] alu_1_tsto_out, DP___2___DP___3_q, LC___5_q, multiplexer_1_out, multiplexer_2_out, PC___1_q,
       SP___6___SP___7_q;
  wire [31:0] controllersim_1_counter;

  Button button_1 (.out(button_1_out));
  Keyboard #(.buflen(32), .trigger("rising")) keyboard_1 (
    .clk(button_1_out), .data(keyboard_1_data));  // open: re, clr, avail
  TTY #(.rows(8), .cols(32), .trigger("rising")) tty_1 (
    .data(alu_1_res[6:0]), .clk(demultiplexer_1_out4));  // open: we, clr
  Register #(.width(16), .trigger("rising")) LC___5 (
    .D({alu_1_res_2, alu_1_res}), .Q(LC___5_q), .clk(demultiplexer_1_out5));  // open: en, clr
  // Probe on demultiplexer_1_out4
  Register #(.width(16), .trigger("rising")) PC___1 (
    .D({alu_1_res_2, alu_1_res}), .Q(PC___1_q), .clk(demultiplexer_1_out1));  // open: en, clr
  // Probe on {{9{1'b0}}, keyboard_1_data}
  ROM #(.addrWidth(16), .dataWidth(8)) rom_1 (.addr(PC___1_q), .data(rom_1_data));  // open: sel
  Demultiplexer #(.select(3), .width(1), .tristate("false")) demultiplexer_1 (
    .out1(demultiplexer_1_out1), .out2(demultiplexer_1_out2), .out3(demultiplexer_1_out3),
    .out4(demultiplexer_1_out4), .out5(demultiplexer_1_out5), .out6(demultiplexer_1_out6),
    .out7(demultiplexer_1_out7), .in(controllersim_1_wclk), .sel(controllersim_1_opnd));  // open: out0
  // Probe on rom_1_data
  // Probe on button_1_out
  Register #(.width(16), .trigger("rising")) SP___6___SP___7 (
    .D({alu_1_res_2, alu_1_res}), .Q(SP___6___SP___7_q), .clk(demultiplexer_1_out6));  // open: en, clr
  // Probe on controllersim_1_rclk
  // Probe on controllersim_1_wclk
  ControllerSim controllersim_1 (
    .NZ(alu_1_nz), .Opcode(rom_1_data), .Halt(button_1_out), .WCLK(controllersim_1_wclk),
    .RCLK(controllersim_1_rclk), .Halted(controllersim_1_halted), .Counter(controllersim_1_counter),
    .Cycle(controllersim_1_cycle), .OPND(controllersim_1_opnd), .OPR(controllersim_1_opr),
    .ART_PAR(controllersim_1_art_par));
  // Probe on controllersim_1_cycle
  // Probe on controllersim_1_counter
  LED #(.active("true")) Halted (.in(controllersim_1_halted));
  Register #(.width(16), .trigger("rising")) DP___2___DP___3 (
    .D({alu_1_res_2, alu_1_res}), .Q(DP___2___DP___3_q), .clk(demultiplexer_1_out2));  // open: en, clr
  Multiplexer #(.select(1), .width(16)) multiplexer_1 (
    .in0(DP___2___DP___3_q), .in1(SP___6___SP___7_q), .out(multiplexer_1_out), .sel(controllersim_1_opnd[2]));
  or or_1 (or_1_out, demultiplexer_1_out3, demultiplexer_1_out7);
  // Probe on controllersim_1_opnd
  and and_1 (and_1_out, or_1_out, controllersim_1_wclk);
  not not_1 (not_1_out, and_1_out);
  // Probe on alu_1_tsto_out
  // Probe on multiplexer_2_out
  Multiplexer #(.select(3), .width(16)) multiplexer_2 (
    .in0({{9{1'b0}}, keyboard_1_data}), .in1(PC___1_q), .in2(DP___2___DP___3_q),
    .in3({{8{1'b0}}, controlled_buffer_2_out}), .in5(LC___5_q), .in6(SP___6___SP___7_q),
    .in7({{8{1'b0}}, controlled_buffer_2_out}), .out(multiplexer_2_out), .sel(controllersim_1_opnd));  // open: in4
  // Probe on controllersim_1_opr
  // Probe on controllersim_1_art_par
  assign controlled_buffer_1_out = and_1_out ? alu_1_res : 8'bz;  // Controlled_Buffer controlled_buffer_1
  RAM #(.addrWidth(16), .dataWidth(8), .bus("asynch")) ram_1 (
    .addr(multiplexer_1_out), .data(controlled_buffer_1_out), .ld(not_1_out));  // open: sel, clr
  assign controlled_buffer_2_out = not_1_out ? controlled_buffer_1_out : 8'bz;  // Controlled_Buffer controlled_buffer_2
  // Probe on controlled_buffer_2_out
  ALU alu_1 (
    .PAR(multiplexer_2_out), .ART_PAR(controllersim_1_art_par), .OP(controllersim_1_opr),
    .TSTO_OUT(alu_1_tsto_out), .clk(controllersim_1_rclk), .NZ(alu_1_nz), .RES({alu_1_res_2, alu_1_res}));
  // Probe on alu_1_nz
  // Probe on {alu_1_res_2, alu_1_res}

  // Notes on the sheet:
  //   INPUT DRIVER
  //   PROGRAM ROM
  //   contents of rom_1 (hex, n*v repeats v):
  //   3e 10*2b 3e 2b 3e 2b 5b 5b 5*2b 5b 3e 8*2b 3c 2d 5d 3e 2e 3c 6*2b 5b 3e 8*2d 3c 2d 5d 2b 3c 3c 3c 5d
  //   3e 2e 3e 3e 5b 5b 2d 5d 3c 5b 3e 2b 3c 2d 5d 3e 3e 5b 3c 3c 2b 3e 2b 3e 2d 5d 3c 5b 3e 2b 3c 2d 5b
  //   3e 2b 3c 2d 5b 3e 2b 3c 2d 5b 3e 2b 3c 2d 5b 3e 2b 3c 2d 5b 3e 2b 3c 2d 5b 3e 2b 3c 2d 5b 3e 2b 3c
  //   2d 5b 3e 2b 3c 2d 5b 3e 5b 2d 5d 3e 2b 3e 2b 3c 3c 3c 2d 5b 3e 2b 3c 2d 11*5d 2b 3e 3e 3e 5d 3c 3c
  //   3c 5d
  //   CONTROL UNIT
  //   DATA RAM
endmodule

module ALU (
  input  [15:0] PAR,
  input  ART_PAR,
  input  [1:0] OP,
  input  clk,
  output [15:0] TSTO_OUT,
  output NZ,
  output [15:0] RES
);

  wire adder_1_cout, adder_2_cout, adder_3_cout, or_1_out, or_2_out;
  wire [3:0] adder_1_out, adder_2_out, adder_3_out, adder_4_out;

  or or_1 (or_1_out, 1'b0, RES[0], RES[1], RES[2], RES[3], RES[4], RES[5], RES[6], RES[7]);
  or or_2 (or_2_out, 1'b0, RES[8], RES[9], RES[10], RES[11], RES[12], RES[13], RES[14], RES[15]);
  or or_3 (NZ, or_1_out, or_2_out);
  Adder #(.width(4)) adder_1 (
    .a(PAR[3:0]), .b({{3{ART_PAR}}, 1'b1}), .out(adder_1_out), .cin(1'b0), .cout(adder_1_cout));
  Adder #(.width(4)) adder_2 (
    .a(PAR[7:4]), .b({4{ART_PAR}}), .out(adder_2_out), .cin(adder_1_cout), .cout(adder_2_cout));
  Adder #(.width(4)) adder_3 (
    .a(PAR[11:8]), .b({4{ART_PAR}}), .out(adder_3_out), .cin(adder_2_cout), .cout(adder_3_cout));
  Adder #(.width(4)) adder_4 (.a(PAR[15:12]), .b({4{ART_PAR}}), .out(adder_4_out), .cin(adder_3_cout));  // open: cout
  Multiplexer #(.select(2), .width(16)) multiplexer_1 (
    .in0(PAR), .in1({adder_4_out, adder_3_out, adder_2_out, adder_1_out}), .in2({PAR[7:0], PAR[15:8]}),
    .in3({RES[15:8], PAR[7:0]}), .out(TSTO_OUT), .sel(OP));
  Register #(.width(16), .trigger("rising")) BUF (.D(TSTO_OUT), .Q(RES), .clk(clk));  // open: en, clr

  // Notes on the sheet:
  //   NZ
  //   NOP
  //   ART
  //   SWP
  //   LOW
  //   ART
  //   SWP
  //   LOW
  //   NOP
  //   LOW
endmodule

module xx (
  input  [7:0] D,
  input  en,
  input  clk,
  output [7:0] Q
);

  wire [7:0] multiplexer_1_out;

  Multiplexer #(.select(1), .width(8)) multiplexer_1 (.in0(Q), .in1(D), .out(multiplexer_1_out), .sel(en));
  Register #(.width(8), .trigger("rising")) register_1 (.D(multiplexer_1_out), .Q(Q), .clk(clk));  // open: en, clr
endmodule

module Controller (
  input  [3:0] Opcode,
  input  Halt,
  output WCLK,
  output RCLK,
  output [1:0] selOperand,
  output fDec,
  output Halted,
  output [7:0] Counter,
  output [1:0] Cycle
);

  wire and_1_out, and_2_out, and_3_out, clock_1_out, d_ff_1_qn, decoder_1_out0, decoder_1_out1,
       decoder_2_out0, demultiplexer_1_out0, demultiplexer_1_out1, multiplexer_1_out, not_1_out, not_2_out,
       not_3_out, not_4_out, or_1_out, t_ff_1_qn, xnor_1_out;
  wire [2:2] multiplexer_2_out;

  T_Flip_Flop #(.trigger("rising")) t_ff_1 (
    .clk(multiplexer_1_out), .T(1'b1), .Q(Halted), .Qn(t_ff_1_qn));  // open: preset, reset, en
  Multiplexer #(.select(1), .width(1)) multiplexer_1 (
    .in0(decoder_2_out0), .in1(Halt), .out(multiplexer_1_out), .sel(Halted));
  Clock #(.highDuration(1), .lowDuration(1)) clock_1 (.out(clock_1_out));
  and and_1 (and_1_out, clock_1_out, t_ff_1_qn);
  not not_1 (not_1_out, clock_1_out);
  and and_2 (and_2_out, decoder_2_out0, not_2_out);
  not not_2 (not_2_out, and_3_out);
  and and_3 (and_3_out, or_1_out, not_3_out);
  not not_3 (not_3_out, d_ff_1_qn);
  D_Flip_Flop #(.trigger("rising")) d_ff_1 (
    .clk(not_1_out), .D(and_2_out), .Qn(d_ff_1_qn));  // open: Q, preset, en, reset
  Demultiplexer #(.select(1), .width(1), .tristate("false")) demultiplexer_1 (
    .out0(demultiplexer_1_out0), .out1(demultiplexer_1_out1), .in(and_1_out), .sel(d_ff_1_qn));
  not not_4 (not_4_out, or_1_out);
  or or_1 (or_1_out, demultiplexer_1_out0, demultiplexer_1_out1);
  Counter #(.width(2), .max('h3), .ongoal("wrap"), .trigger("rising")) counter_1 (
    .Q(Cycle), .clk(demultiplexer_1_out1));  // open: load, D, count, carry, clr
  and and_4 (WCLK, not_4_out, decoder_1_out0);
  and and_5 (RCLK, not_4_out, decoder_1_out1);
  Decoder #(.select(1), .tristate("false")) decoder_1 (.out0(decoder_1_out0), .out1(decoder_1_out1), .sel(Cycle[0]));
  xnor xnor_1 (xnor_1_out, Cycle[0], Cycle[1]);
  Multiplexer #(.select(1), .width(4)) multiplexer_2 (
    .in0(Opcode), .in1(4'b0001), .out({fDec, multiplexer_2_out[2], selOperand}), .sel(xnor_1_out));
  Decoder #(.select(2), .tristate("false")) decoder_2 (
    .out0(decoder_2_out0), .sel(selOperand));  // open: out1, out2, out3
  // Probe on selOperand
  Counter #(.width(8), .max('hff), .ongoal("wrap"), .trigger("rising")) counter_2 (
    .Q(Counter), .clk(demultiplexer_1_out1));  // open: load, D, count, carry, clr
endmodule

module ControllerSim (
  input  NZ,
  input  [7:0] Opcode,
  input  Halt,
  output WCLK,
  output RCLK,
  output [2:0] OPND,
  output [1:0] OPR,
  output ART_PAR,
  output [31:0] Counter,
  output [7:0] Cycle,
  output Halted
);

  wire and_1_out, clock_1_out, END_q, multiplexer_1_out, multiplexer_2_out, not_1_out, not_2_out, t_ff_1_qn;
  wire [7:0] OPCODE_q;
  wire [7:7] rom_1_data_2;
  wire [11:0] rom_1_data;

  not not_1 (not_1_out, Halt);
  Multiplexer #(.select(1), .width(1)) multiplexer_1 (
    .in0(Cycle[7]), .in1(NZ), .out(multiplexer_1_out), .sel(rom_1_data[1]));
  Register #(.width(8), .trigger("rising")) u_OPCODE (
    .D({rom_1_data_2[7], Opcode[6:0]}), .en(1'b1), .Q(OPCODE_q), .clk(END_q));  // open: clr
  Multiplexer #(.select(1), .width(1)) multiplexer_2 (
    .in0(not_1_out), .in1(rom_1_data[3]), .out(multiplexer_2_out), .sel(t_ff_1_qn));
  D_Flip_Flop #(.trigger("rising")) JMP (
    .clk(and_1_out), .D(multiplexer_1_out), .Q(Cycle[7]), .reset(END_q));  // open: Qn, preset, en
  Counter #(.width(7), .max('h7f), .ongoal("wrap"), .trigger("rising")) uPC (
    .Q(Cycle[6:0]), .clk(and_1_out), .clr(END_q));  // open: load, D, count, carry
  D_Flip_Flop #(.trigger("rising")) END (.clk(and_1_out), .D(rom_1_data[0]), .Q(END_q));  // open: Qn, preset, en, reset
  and and_1 (and_1_out, clock_1_out, t_ff_1_qn);
  Clock #(.highDuration(1), .lowDuration(1)) clock_1 (.out(clock_1_out));
  T_Flip_Flop #(.trigger("rising")) t_ff_1 (
    .clk(multiplexer_2_out), .T(1'b1), .Q(Halted), .Qn(t_ff_1_qn));  // open: preset, reset, en
  ROM #(.addrWidth(16), .dataWidth(12)) rom_1 (
    .addr({OPCODE_q, Cycle}),
    .data({rom_1_data[11:10], OPND, OPR, ART_PAR, rom_1_data[3], rom_1_data_2[7], rom_1_data[1:0]}));  // open: sel
  Counter #(.width(32), .max('hffffffff), .ongoal("wrap"), .trigger("rising")) counter_1 (
    .Q(Counter), .clk(and_1_out));  // open: load, D, count, carry, clr
  and and_2 (WCLK, not_2_out, rom_1_data[11]);
  not not_2 (not_2_out, and_1_out);
  and and_3 (RCLK, not_2_out, rom_1_data[10]);

  // Notes on the sheet:
  //   contents of rom_1 (hex, n*v repeats v):
  //   1 255*0 4a0 881 10750*0 5a0 980 4a0 881 252*0 8 400 980 4a0 881 251*0 5b0 980 4a0 881 252*0 580 a00
  //   4a0 881 3580*0 530 900 4a0 881 508*0 520 900 4a0 881 7420*0 582 6a0 a80 4a0 885 124*0 730 b00 480
  //   b80 730 b00 7e0 b80 4a0 881 373*0 7c0 880 720 b00 480 7e0 880 720 b01 19959*0 4a0 885 254*0 4a0 885
  //   254*0 4a0 885 254*0 4a0 885 3582*0 4a0 885 510*0 4a0 885 7422*0 6a0 a80 4a0 885 508*0 6b0 a82 4a0
  //   881 126*0 4a0 885
endmodule
